# Fritzing sketch HC_SR04_control_circuit (saved by Fritzing 0.9.2b)
breadboards: 1

parts:
  Part1 = Arduino Uno (Rev3)
  R1 = Resistor [tolerance=±5% resistance=220 package=THT]
  LED1 = LED - 5mm [color="Red (633nm)" package="5 mm [THT]"]
  Part2 = SRF05 Ultrasonic Rangefinder

nets:
  N1: Part1.D12/MISO, Part2.Echo
  N2: Part1.D13/SCK, Part2.Trig
  N3: Part1.D3_PWM, R1.Pin_0
  5V: Part1.5V, Part2.VCC
  GND: Part1.GND, R1.Pin_1, LED1.cathode, LED1.anode, Part2.GND
