# Fritzing sketch HC_SR04_test_circuit (saved by Fritzing 0.9.2b)

parts:
  Part1 = Arduino Uno (Rev3)
  Part2 = SRF05 Ultrasonic Rangefinder

nets:
  N1: Part1.D11_PWM/MOSI, Part2.Echo
  N2: Part1.D12/MISO, Part2.Trig
  5V: Part1.5V, Part2.VCC
  GND: Part1.GND, Part2.GND
