# Fritzing sketch Heli_controller_mine_circuit (saved by Fritzing 0.9.2b)
breadboards: 1

parts:
  Part1 = Arduino Uno (Rev3)
  R1 = Resistor [tolerance=±5% resistance=220 package=THT]
  LED1 = LED - 5mm [color="Red (633nm)" package="5 mm [THT]"]
  R2 = Rotary Potentiometer (Small) [maximum_resistance=100kΩ package=THT]
  R3 = Rotary Potentiometer (Small) [maximum_resistance=100kΩ package=THT]
  R4 = Rotary Potentiometer (Small) [maximum_resistance=100kΩ package=THT]

nets:
  N1: Part1.A0, R4.leg2
  N2: Part1.A1, R3.leg2
  N3: Part1.A2, R2.leg2
  N4: Part1.D3_PWM, R1.Pin_0
  N5: Part1.5V, R2.leg1, R3.leg1, R4.leg1
  N6: Part1.GND, R1.Pin_1, LED1.cathode, LED1.anode, R2.wiper, R3.wiper, R4.wiper
