# Fritzing sketch SwarmBot (saved by Fritzing 0.9.2b)
breadboards: 1

parts:
  BATT1 = LiPoly Battery (1300mAh)
  Part1 = PowerBoost 500 Charger
  Part2 = SRF05 Ultrasonic Rangefinder
  BB1 = 8-Line Bi-Directional Level Shifter
  3_3V_regulator = Voltage Regulator [package=to220-adj]
  Part3 = Arduino Pro Mini v13
  330_or_so = Resistor [tolerance=±5% resistance=220 package=THT]
  IR_LED = LED - 5mm [color="Red (633nm)" package="5 mm [THT]"]

nets:
  N1: BATT1.positive, Part1.VBAT, 3_3V_regulator.IN
  GND: BATT1.negative, Part1.GND, Part2.GND, BB1.no_name_yet#20, 3_3V_regulator.ADJ
  N2: Part1.5.0V, Part2.VCC, BB1.no_name_yet#11
  N3: Part2.Trig, BB1.no_name_yet#19
  N4: Part2.Echo, BB1.no_name_yet#18
  N5: BB1.no_name_yet#1, 3_3V_regulator.OUT, Part3.VCC
  N6: BB1.no_name_yet#8, Part3.D4
  N7: BB1.no_name_yet#9, Part3.D5_PWM
  N8: Part3.D3_PWM, 330_or_so.Pin_1, IR_LED.cathode, IR_LED.anode

custom parts:
  LiPoly Battery (1300mAh): Lithium Ion Polymer Battery (1300mAh)
  PowerBoost 500 Charger: The PowerBoost 500C is a little DC/DC boost converter module that can be powered by any 3.7V LiIon/LiPoly battery, and convert the battery output to 5.2V DC for running your 5V projects. At its heart is a TPS61090 boost converter from TI. This boost converter chip has some really nice extras such as low battery detection, 2A internal switch, synchronous conversion, excellent efficiency, and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
  8-Line Bi-Directional Level Shifter: 8-channel Bi-Directional Level Shifter with TXB0108
